// Logisim project cpu.circ as structural Verilog: 2 circuits, main circuit CPU
module CPU (
  input  [31:0] Instruction,
  input  CLK,
  output [31:0] s0,
  output [31:0] s1,
  output [31:0] t0,
  output [31:0] t1,
  output [31:0] a0,
  output [31:0] ra,
  output [31:0] sp,
  output [31:0] PC
);

  wire [31:0] IMM, multiplexer_1_out, regfile_1_r1, regfile_1_r2;

  // Incrementer incrementer_1: pin names not known
  // PC pc_1: pin names not known
  RegFile regfile_1 (
    .Clk(CLK), .R1(regfile_1_r1), .R2(regfile_1_r2),
    .RD({Instruction[7], Instruction[8], Instruction[9], Instruction[10], Instruction[11]}),
    .RS1({Instruction[15], Instruction[16], Instruction[17], Instruction[18], Instruction[19]}),
    .RS2({Instruction[20], Instruction[21], Instruction[22], Instruction[23], Instruction[24]}), .s0(s0),
    .s1(s1), .t0(t0), .t1(t1), .a0(a0), .ra(ra), .sp(sp));  // open: WE, W
  Multiplexer #(.width(32)) multiplexer_1 (.in0(regfile_1_r2), .in1(IMM), .out(multiplexer_1_out));  // open: sel, en
  ALU alu_1 (.A(regfile_1_r1), .B(multiplexer_1_out));  // open: ALU_Op, Out
  ImmPeligroso immpeligroso_1 (
    .INST({Instruction[0], Instruction[1], Instruction[2], Instruction[3], Instruction[4], Instruction[5], Instruction[6], Instruction[7], Instruction[8], Instruction[9], Instruction[10], Instruction[11], Instruction[12], Instruction[13], Instruction[14], Instruction[15], Instruction[16], Instruction[17], Instruction[18], Instruction[19], Instruction[20], Instruction[21], Instruction[22], Instruction[23], Instruction[24], Instruction[25], Instruction[26], Instruction[27], Instruction[28], Instruction[29], Instruction[30], Instruction[31]}),
    .IMM(IMM),
    .OPCODE({Instruction[0], Instruction[1], Instruction[2], Instruction[3], Instruction[4], Instruction[5], Instruction[6]}));
  // memory_main main_1: pin names not known

  // Other names for the same wires on the sheet: fetch_addr[31:0] = PC;
  //   F7[6:0] = {Instruction[25], Instruction[26], Instruction[27], Instruction[28], Instruction[29], Instruction[30], Instruction[31]};
  //   INST[31:0] = Instruction;
  //   INST_INV[31:0] = {Instruction[0], Instruction[1], Instruction[2], Instruction[3], Instruction[4], Instruction[5], Instruction[6], Instruction[7], Instruction[8], Instruction[9], Instruction[10], Instruction[11], Instruction[12], Instruction[13], Instruction[14], Instruction[15], Instruction[16], Instruction[17], Instruction[18], Instruction[19], Instruction[20], Instruction[21], Instruction[22], Instruction[23], Instruction[24], Instruction[25], Instruction[26], Instruction[27], Instruction[28], Instruction[29], Instruction[30], Instruction[31]};
  //   RS2[4:0] = {Instruction[20], Instruction[21], Instruction[22], Instruction[23], Instruction[24]};
  //   RS1[4:0] = {Instruction[15], Instruction[16], Instruction[17], Instruction[18], Instruction[19]};
  //   F3[2:0] = {Instruction[12], Instruction[13], Instruction[14]};
  //   RD[4:0] = {Instruction[7], Instruction[8], Instruction[9], Instruction[10], Instruction[11]};
  //   OPCODE[6:0] = {Instruction[0], Instruction[1], Instruction[2], Instruction[3], Instruction[4], Instruction[5], Instruction[6]}

  // Notes on the sheet:
  //   NOTE
  //   Please do not modify/replace/move/change/delete/etc input and output pins
  //   These are debug/test outputs from your circuit
endmodule

module ImmPeligroso (
  input  [31:0] INST,
  input  [6:0] OPCODE,
  output [31:0] IMM
);

  wire [31:0] TIPO_B, TIPO_I, TIPO_J, TIPO_S;

  assign TIPO_I = {{20{INST[11]}}, INST[11:0]};  // Bit_Extender bit_extender_1
  assign TIPO_S = {{20{INST[6]}}, {INST[6:0], INST[24:20]}};  // Bit_Extender bit_extender_2
  assign TIPO_B = {{19{INST[0]}}, {INST[0], INST[24], INST[6:1], INST[23:20], 1'b0}};  // Bit_Extender bit_extender_3
  assign TIPO_J = {{11{INST[0]}}, {INST[0], INST[19:1], 1'b0}};  // Bit_Extender bit_extender_4
  Multiplexer #(.select(3), .width(32)) multiplexer_1 (
    .in0(TIPO_I), .in1(TIPO_S), .in2(TIPO_B), .in3({INST[19:0], {12{1'b0}}}), .in4(TIPO_J));  // open: in5, in6, in7, out, sel, en
  Comparator comparator_1 ();  // open: a, b, gt, eq, lt

  // Other names for the same wires on the sheet: TIPO_U[31:12] = INST[19:0]
endmodule
